// Digital circuit MMU.dig as structural Verilog
module MMU (
  input  [7:0] DATA,
  input  [15:0] ADDRESS,
  input  MREAD,
  input  MWRITE,
  input  [7:0] IN_0,
  input  [7:0] IN_1,
  input  [7:0] IN_2,
  input  [7:0] IN_3,
  input  [7:0] IN_4,
  input  [7:0] IN_5,
  input  [7:0] IN_6,
  input  [7:0] IN_7,
  input  INT_0,
  input  INT_1,
  input  INT_2,
  input  INT_3,
  input  P0,
  input  RST,
  input  iv_o,
  input  ei,
  output [7:0] LED_R0,
  output [7:0] LED_R1,
  output [7:0] LED_R2,
  output [7:0] LED_R3,
  output [7:0] LED_R4,
  output [7:0] LED_R5,
  output [7:0] LED_R6,
  output [7:0] LED_R7,
  output IRQ
);

  wire _74138_1_pin13, _74138_1_pin14, _74138_1_pin15, _74138_2_pin14, _74138_2_pin15, _74138_3_pin7,
       _74138_3_pin9, _74138_3_pin10, _74138_3_pin11, _74138_3_pin12, _74138_3_pin13, _74138_3_pin14,
       _74138_3_pin15, _74138_4_pin7, _74138_4_pin9, _74138_4_pin10, _74138_4_pin11, _74138_4_pin12,
       _74138_4_pin13, _74138_4_pin14, _74138_4_pin15, _74573_1_pin16, _74573_1_pin17, _74573_1_pin18,
       _74573_1_pin19, _74573_5_pin1, and_1_out, and_2_out, and_3_out, and_4_out, and_5_out, and_6_out,
       and_7_out, and_8_out, nor_1_out, nor_2_out, nor_3_out, nor_4_out, nor_5_out, nor_6_out, nor_7_out,
       nor_8_out, nor_9_out, nor_10_out, nor_11_out, not_1_out, not_2_out, not_3_out, not_4_out, not_5_out,
       not_6_out, not_7_out, not_8_out, not_9_out, not_10_out, not_11_out, or_1_out, or_2_out, or_3_out,
       or_4_out, or_5_out, or_6_out, or_7_out, or_8_out, or_9_out, or_10_out, or_11_out, or_12_out, or_13_out;

  not not_1 (not_1_out, iv_o);
  and and_1 (and_1_out, _74573_1_pin19, not_1_out);
  and and_2 (and_2_out, _74573_1_pin18, not_1_out);
  and and_3 (and_3_out, _74573_1_pin17, not_1_out);
  and and_4 (and_4_out, _74573_1_pin16, not_1_out);
  or or_1 (or_1_out, and_1_out, RST);
  or or_2 (or_2_out, and_2_out, RST);
  or or_3 (or_3_out, and_3_out, RST);
  or or_4 (or_4_out, and_4_out, RST);
  nor nor_1 (nor_1_out, or_1_out, nor_2_out);
  nor nor_2 (nor_2_out, nor_1_out, INT_0);
  nor nor_3 (nor_3_out, or_2_out, nor_4_out);
  nor nor_4 (nor_4_out, nor_3_out, INT_1);
  nor nor_5 (nor_5_out, or_3_out, nor_6_out);
  nor nor_6 (nor_6_out, nor_5_out, INT_2);
  nor nor_7 (nor_7_out, or_4_out, nor_8_out);
  nor nor_8 (nor_8_out, nor_7_out, INT_3);
  _74138 _74138_1 (
    .pin1(ADDRESS[13]), .pin2(ADDRESS[14]), .pin3(ADDRESS[15]), .pin4(1'b0), .pin5(1'b0), .pin6(1'b1),
    .pin8(1'b0), .pin13(_74138_1_pin13), .pin14(_74138_1_pin14), .pin15(_74138_1_pin15), .pin16(1'b1));  // open: pin7, pin9, pin10, pin11, pin12
  not not_2 (not_2_out, nor_1_out);
  and and_5 (and_5_out, _74138_1_pin15, _74138_1_pin14);
  and and_6 (and_6_out, not_2_out, nor_3_out);
  or or_5 (or_5_out, nor_1_out, nor_3_out);
  not not_3 (not_3_out, or_5_out);
  RAMSinglePortSel #(.AddrBits(15), .isProgramMemory("true"), .Bits(8)) ramsingleportsel_1 (
    .A(ADDRESS[14:0]), .CS(ADDRESS[15]), .WE(not_4_out), .OE(not_5_out), .D(DATA));
  not not_4 (not_4_out, MWRITE);
  and and_7 (and_7_out, not_3_out, nor_5_out);
  or or_6 (or_6_out, or_5_out, nor_5_out);
  not not_5 (not_5_out, MREAD);
  not not_6 (not_6_out, ei);
  not not_7 (not_7_out, or_6_out);
  ROM #(.AddrBits(14), .isProgramMemory("true"), .Bits(8)) rom_1 (.A(ADDRESS[13:0]), .sel(nor_9_out), .D(DATA));
  and and_8 (and_8_out, not_7_out, nor_7_out);
  nor nor_9 (nor_9_out, MREAD, and_5_out);
  _74573 _74573_1 (
    .pin1(1'b0), .pin2(nor_1_out), .pin3(and_6_out), .pin4(and_7_out), .pin5(and_8_out), .pin6(1'b0),
    .pin7(1'b0), .pin8(1'b0), .pin9(1'b0), .pin10(1'b0), .pin11(P0), .pin16(_74573_1_pin16),
    .pin17(_74573_1_pin17), .pin18(_74573_1_pin18), .pin19(_74573_1_pin19), .pin20(1'b1));  // open: pin12, pin13, pin14, pin15
  _74138 _74138_2 (
    .pin1(ADDRESS[10]), .pin2(ADDRESS[11]), .pin3(ADDRESS[12]), .pin4(_74138_1_pin13), .pin5(1'b0),
    .pin6(1'b1), .pin8(1'b0), .pin14(_74138_2_pin14), .pin15(_74138_2_pin15), .pin16(1'b1));  // open: pin7, pin9, pin10, pin11, pin12, pin13
  not not_8 (not_8_out, _74573_1_pin19);
  or or_7 (or_7_out, not_8_out, iv_o);
  _74573 _74573_2 (
    .pin1(or_7_out), .pin2(1'b0), .pin3(1'b0), .pin4(1'b0), .pin5(1'b0), .pin6(1'b0), .pin7(1'b0),
    .pin8(1'b0), .pin9(1'b0), .pin10(1'b0), .pin11(1'b1), .pin12(DATA[7]), .pin13(DATA[6]), .pin14(DATA[5]),
    .pin15(DATA[4]), .pin16(DATA[3]), .pin17(DATA[2]), .pin18(DATA[1]), .pin19(DATA[0]), .pin20(1'b1));
  or or_8 (or_8_out, _74573_1_pin19, _74573_1_pin18);
  or or_9 (or_9_out, _74573_1_pin17, _74573_1_pin16);
  _74138 _74138_3 (
    .pin1(ADDRESS[0]), .pin2(ADDRESS[1]), .pin3(ADDRESS[2]), .pin4(_74138_2_pin15), .pin5(1'b0), .pin6(1'b1),
    .pin7(_74138_3_pin7), .pin8(1'b0), .pin9(_74138_3_pin9), .pin10(_74138_3_pin10), .pin11(_74138_3_pin11),
    .pin12(_74138_3_pin12), .pin13(_74138_3_pin13), .pin14(_74138_3_pin14), .pin15(_74138_3_pin15),
    .pin16(1'b1));
  _74138 _74138_4 (
    .pin1(ADDRESS[0]), .pin2(ADDRESS[1]), .pin3(ADDRESS[2]), .pin4(_74138_2_pin14), .pin5(MREAD),
    .pin6(1'b1), .pin7(_74138_4_pin7), .pin8(1'b0), .pin9(_74138_4_pin9), .pin10(_74138_4_pin10),
    .pin11(_74138_4_pin11), .pin12(_74138_4_pin12), .pin13(_74138_4_pin13), .pin14(_74138_4_pin14),
    .pin15(_74138_4_pin15), .pin16(1'b1));
  or or_10 (or_10_out, RST, not_1_out);
  nor nor_10 (nor_10_out, or_10_out, nor_11_out);
  nor nor_11 (nor_11_out, nor_10_out, not_6_out);
  or or_11 (or_11_out, or_8_out, or_9_out);
  not not_9 (not_9_out, _74573_1_pin18);
  or or_12 (or_12_out, not_9_out, iv_o);
  _74573 _74573_3 (
    .pin1(or_12_out), .pin2(1'b0), .pin3(1'b0), .pin4(1'b0), .pin5(1'b0), .pin6(1'b1), .pin7(1'b0),
    .pin8(1'b0), .pin9(1'b0), .pin10(1'b0), .pin11(1'b1), .pin12(DATA[7]), .pin13(DATA[6]), .pin14(DATA[5]),
    .pin15(DATA[4]), .pin16(DATA[3]), .pin17(DATA[2]), .pin18(DATA[1]), .pin19(DATA[0]), .pin20(1'b1));
  and and_9 (IRQ, nor_10_out, or_11_out);
  Register #(.Bits(8)) register_1 (.D(DATA), .C(~MWRITE), .en(~_74138_3_pin15), .Q(LED_R0));
  Register #(.Bits(8)) register_2 (.D(DATA), .C(~MWRITE), .en(~_74138_3_pin14), .Q(LED_R1));
  Register #(.Bits(8)) register_3 (.D(DATA), .C(~MWRITE), .en(~_74138_3_pin13), .Q(LED_R2));
  Register #(.Bits(8)) register_4 (.D(DATA), .C(~MWRITE), .en(~_74138_3_pin12), .Q(LED_R3));
  Register #(.Bits(8)) register_5 (.D(DATA), .C(~MWRITE), .en(~_74138_3_pin11), .Q(LED_R4));
  Register #(.Bits(8)) register_6 (.D(DATA), .C(~MWRITE), .en(~_74138_3_pin10), .Q(LED_R5));
  Register #(.Bits(8)) register_7 (.D(DATA), .C(~MWRITE), .en(~_74138_3_pin9), .Q(LED_R6));
  Register #(.Bits(8)) register_8 (.D(DATA), .C(~MWRITE), .en(~_74138_3_pin7), .Q(LED_R7));
  assign DATA = ~_74138_4_pin15 ? IN_0 : 8'bz;  // DriverInvSel driverinvsel_1
  assign DATA = ~_74138_4_pin14 ? IN_1 : 8'bz;  // DriverInvSel driverinvsel_2
  assign DATA = ~_74138_4_pin13 ? IN_2 : 8'bz;  // DriverInvSel driverinvsel_3
  assign DATA = ~_74138_4_pin12 ? IN_3 : 8'bz;  // DriverInvSel driverinvsel_4
  assign DATA = ~_74138_4_pin11 ? IN_4 : 8'bz;  // DriverInvSel driverinvsel_5
  assign DATA = ~_74138_4_pin10 ? IN_5 : 8'bz;  // DriverInvSel driverinvsel_6
  assign DATA = ~_74138_4_pin9 ? IN_6 : 8'bz;  // DriverInvSel driverinvsel_7
  assign DATA = ~_74138_4_pin7 ? IN_7 : 8'bz;  // DriverInvSel driverinvsel_8
  not not_10 (not_10_out, _74573_1_pin17);
  or or_13 (or_13_out, not_10_out, iv_o);
  _74573 _74573_4 (
    .pin1(or_13_out), .pin2(1'b0), .pin3(1'b0), .pin4(1'b0), .pin5(1'b0), .pin6(1'b0), .pin7(1'b1),
    .pin8(1'b0), .pin9(1'b0), .pin10(1'b0), .pin11(1'b1), .pin12(DATA[7]), .pin13(DATA[6]), .pin14(DATA[5]),
    .pin15(DATA[4]), .pin16(DATA[3]), .pin17(DATA[2]), .pin18(DATA[1]), .pin19(DATA[0]), .pin20(1'b1));
  _74573 _74573_5 (
    .pin1(_74573_5_pin1), .pin2(1'b0), .pin3(1'b0), .pin4(1'b0), .pin5(1'b0), .pin6(1'b1), .pin7(1'b1),
    .pin8(1'b0), .pin9(1'b0), .pin10(1'b0), .pin11(1'b1), .pin12(DATA[7]), .pin13(DATA[6]), .pin14(DATA[5]),
    .pin15(DATA[4]), .pin16(DATA[3]), .pin17(DATA[2]), .pin18(DATA[1]), .pin19(DATA[0]), .pin20(1'b1));
  not not_11 (not_11_out, _74573_1_pin16);
  or or_14 (_74573_5_pin1, not_11_out, iv_o);

  // Notes on the sheet:
  //   DATA: pin 1
  //   ADDRESS: pin 4
  //   MREAD: pin 2, default 1
  //   MWRITE: pin 3, default 1
  //   LED_R0: pin 32
  //   LED_R1: pin 31
  //   LED_R2: pin 30
  //   LED_R3: pin 29
  //   LED_R4: pin 28
  //   LED_R5: pin 27
  //   LED_R6: pin 26
  //   LED_R7: pin 25
  //   IN_0: pin 24
  //   IN_1: pin 23
  //   IN_2: pin 22
  //   IN_3: pin 21
  //   IN_4: pin 20
  //   IN_5: pin 19
  //   IN_6: pin 18
  //   IN_7: pin 17
  //   INT_0: pin 7
  //   INT_1: pin 8
  //   INT_2: pin 9
  //   INT_3: pin 10
  //   P0: pin 6
  //   RST: pin 5
  //   IRQ: pin 11
  //   iv_o: pin 12, default 1
  //   ei: pin 13, default 1
  //   rom_1 loads leds.s.hex
endmodule
