// Digital circuit alu_board.dig as structural Verilog
module alu_board (
  input  [7:0] DATA,
  input  A_i,
  input  A_o,
  input  ALU_latch,
  input  B_i,
  input  B_o,
  input  [4:0] ALU_OP,
  input  ALU_d,
  input  ALUF_d,
  input  F_o,
  input  F_i,
  output [7:0] DATA_OUT,
  output C,
  output Z,
  output SF,
  output OF,
  output [7:0] DBG_A,
  output [7:0] DBG_B
);

  wire _74573_1_pin12, _74573_1_pin13, _74573_1_pin14, _74573_1_pin15, and_1_out, and_2_out, and_3_out,
       and_4_out, and_5_out, and_6_out, and_7_out, not_1_out, not_2_out, or_3_out;
  wire [7:0] _74573_6_pin6, AROM_low_d;
  wire [12:0] _74573_5_pin12, or_1_out;

  _74573 _74573_1 (
    .pin1(1'b0), .pin2(DATA[0]), .pin3(DATA[1]), .pin4(DATA[2]), .pin5(DATA[3]), .pin6(DATA[4]),
    .pin7(DATA[5]), .pin8(DATA[6]), .pin9(DATA[7]), .pin10(1'b0), .pin11(F_i), .pin12(_74573_1_pin12),
    .pin13(_74573_1_pin13), .pin14(_74573_1_pin14), .pin15(_74573_1_pin15), .pin16(OF), .pin17(SF),
    .pin18(Z), .pin19(C), .pin20(1'b1));
  _74573 _74573_2 (
    .pin1(F_o), .pin2(C), .pin3(Z), .pin4(SF), .pin5(OF), .pin6(_74573_1_pin15), .pin7(_74573_1_pin14),
    .pin8(_74573_1_pin13), .pin9(_74573_1_pin12), .pin10(1'b0), .pin11(1'b1), .pin12(DATA_OUT[7]),
    .pin13(DATA_OUT[6]), .pin14(DATA_OUT[5]), .pin15(DATA_OUT[4]), .pin16(DATA_OUT[3]), .pin17(DATA_OUT[2]),
    .pin18(DATA_OUT[1]), .pin19(DATA_OUT[0]), .pin20(1'b1));
  _74573 _74573_3 (
    .pin1(1'b0), .pin2(DATA[0]), .pin3(DATA[1]), .pin4(DATA[2]), .pin5(DATA[3]), .pin6(DATA[4]),
    .pin7(DATA[5]), .pin8(DATA[6]), .pin9(DATA[7]), .pin10(1'b0), .pin11(A_i), .pin12(DBG_A[7]),
    .pin13(DBG_A[6]), .pin14(DBG_A[5]), .pin15(DBG_A[4]), .pin16(DBG_A[3]), .pin17(DBG_A[2]),
    .pin18(DBG_A[1]), .pin19(DBG_A[0]), .pin20(1'b1));
  _74573 _74573_4 (
    .pin1(A_o), .pin2(DBG_A[0]), .pin3(DBG_A[1]), .pin4(DBG_A[2]), .pin5(DBG_A[3]), .pin6(DBG_A[4]),
    .pin7(DBG_A[5]), .pin8(DBG_A[6]), .pin9(DBG_A[7]), .pin10(1'b0), .pin11(1'b1), .pin12(DATA_OUT[7]),
    .pin13(DATA_OUT[6]), .pin14(DATA_OUT[5]), .pin15(DATA_OUT[4]), .pin16(DATA_OUT[3]), .pin17(DATA_OUT[2]),
    .pin18(DATA_OUT[1]), .pin19(DATA_OUT[0]), .pin20(1'b1));
  or or_1 (or_1_out[12], and_1_out, and_2_out);
  and and_1 (and_1_out, _74573_6_pin6[4], ALU_OP[3]);
  and and_2 (and_2_out, not_1_out, C);
  not not_1 (not_1_out, ALU_OP[3]);
  ROM #(.AddrBits(13), .Bits(8)) AROM_low (.A({or_1_out[12], ALU_OP[3:0], or_1_out[7:0]}), .sel(1'b1), .D(AROM_low_d));
  _74573 _74573_5 (
    .pin1(1'b0), .pin2(DBG_A[0]), .pin3(DBG_A[1]), .pin4(DBG_A[2]), .pin5(DBG_A[3]), .pin6(DBG_A[4]),
    .pin7(DBG_A[5]), .pin8(DBG_A[6]), .pin9(DBG_A[7]), .pin10(1'b0), .pin11(ALU_latch),
    .pin12(_74573_5_pin12[3]), .pin13(_74573_5_pin12[2]), .pin14(_74573_5_pin12[1]),
    .pin15(_74573_5_pin12[0]), .pin16(or_1_out[3]), .pin17(or_1_out[2]), .pin18(or_1_out[1]),
    .pin19(or_1_out[0]), .pin20(1'b1));
  _74573 _74573_6 (
    .pin1(ALU_d), .pin2(AROM_low_d[0]), .pin3(AROM_low_d[1]), .pin4(AROM_low_d[2]), .pin5(AROM_low_d[3]),
    .pin6(_74573_6_pin6[0]), .pin7(_74573_6_pin6[1]), .pin8(_74573_6_pin6[2]), .pin9(_74573_6_pin6[3]),
    .pin10(1'b0), .pin11(1'b1), .pin12(DATA_OUT[7]), .pin13(DATA_OUT[6]), .pin14(DATA_OUT[5]),
    .pin15(DATA_OUT[4]), .pin16(DATA_OUT[3]), .pin17(DATA_OUT[2]), .pin18(DATA_OUT[1]), .pin19(DATA_OUT[0]),
    .pin20(1'b1));
  and and_3 (and_3_out, C, ALU_OP[3]);
  or or_2 (_74573_5_pin12[12], and_3_out, and_4_out);
  and and_4 (and_4_out, not_2_out, AROM_low_d[4]);
  not not_2 (not_2_out, ALU_OP[3]);
  and and_5 (and_5_out, not_2_out, _74573_6_pin6[4]);
  and and_6 (and_6_out, AROM_low_d[4], ALU_OP[3]);
  or or_3 (or_3_out, and_5_out, and_6_out);
  ROM #(.AddrBits(13), .Bits(8)) AROM_high (
    .A({_74573_5_pin12[12], ALU_OP[3:0], _74573_5_pin12[7:0]}), .sel(1'b1), .D(_74573_6_pin6));
  and and_7 (and_7_out, _74573_6_pin6[5], AROM_low_d[5]);
  _74573 _74573_7 (
    .pin1(ALUF_d), .pin2(or_3_out), .pin3(and_7_out), .pin4(_74573_6_pin6[6]), .pin5(_74573_6_pin6[7]),
    .pin6(1'b0), .pin7(1'b0), .pin8(1'b0), .pin9(1'b0), .pin10(1'b0), .pin11(1'b1), .pin12(DATA_OUT[7]),
    .pin13(DATA_OUT[6]), .pin14(DATA_OUT[5]), .pin15(DATA_OUT[4]), .pin16(DATA_OUT[3]), .pin17(DATA_OUT[2]),
    .pin18(DATA_OUT[1]), .pin19(DATA_OUT[0]), .pin20(1'b1));
  _74573 _74573_8 (
    .pin1(1'b0), .pin2(DATA[0]), .pin3(DATA[1]), .pin4(DATA[2]), .pin5(DATA[3]), .pin6(DATA[4]),
    .pin7(DATA[5]), .pin8(DATA[6]), .pin9(DATA[7]), .pin10(1'b0), .pin11(B_i), .pin12(DBG_B[7]),
    .pin13(DBG_B[6]), .pin14(DBG_B[5]), .pin15(DBG_B[4]), .pin16(DBG_B[3]), .pin17(DBG_B[2]),
    .pin18(DBG_B[1]), .pin19(DBG_B[0]), .pin20(1'b1));
  _74573 _74573_9 (
    .pin1(B_o), .pin2(DBG_B[0]), .pin3(DBG_B[1]), .pin4(DBG_B[2]), .pin5(DBG_B[3]), .pin6(DBG_B[4]),
    .pin7(DBG_B[5]), .pin8(DBG_B[6]), .pin9(DBG_B[7]), .pin10(1'b0), .pin11(1'b1), .pin12(DATA_OUT[7]),
    .pin13(DATA_OUT[6]), .pin14(DATA_OUT[5]), .pin15(DATA_OUT[4]), .pin16(DATA_OUT[3]), .pin17(DATA_OUT[2]),
    .pin18(DATA_OUT[1]), .pin19(DATA_OUT[0]), .pin20(1'b1));
  _74573 _74573_10 (
    .pin1(1'b0), .pin2(DBG_B[0]), .pin3(DBG_B[1]), .pin4(DBG_B[2]), .pin5(DBG_B[3]), .pin6(DBG_B[4]),
    .pin7(DBG_B[5]), .pin8(DBG_B[6]), .pin9(DBG_B[7]), .pin10(1'b0), .pin11(ALU_latch),
    .pin12(_74573_5_pin12[7]), .pin13(_74573_5_pin12[6]), .pin14(_74573_5_pin12[5]),
    .pin15(_74573_5_pin12[4]), .pin16(or_1_out[7]), .pin17(or_1_out[6]), .pin18(or_1_out[5]),
    .pin19(or_1_out[4]), .pin20(1'b1));

  // Notes on the sheet:
  //   A_o: default 1
  //   ALU_latch: default 1
  //   B_o: default 1
  //   ALU_d: default 1
  //   ALUF_d: default 1
  //   F_o: default 1
  //   AROM_low loads alu_low.bin.hex
  //   AROM_high loads alu_high.bin.hex
endmodule
