// Digital circuit cpu.dig as structural Verilog
module cpu (
  input  clk
);

  wire alu_board_1_c, alu_board_1_of, alu_board_1_sf, alu_board_1_z, and_1_out, decode_1_a_i, decode_1_a_o,
       decode_1_alu_d, decode_1_alu_latch, decode_1_aluf_d, decode_1_b_i, decode_1_b_o, decode_1_di_iv_o,
       decode_1_ei, decode_1_f_i, decode_1_f_o, decode_1_fault, decode_1_mf_a, decode_1_mh_i, decode_1_mh_o,
       decode_1_ml_i, decode_1_ml_o, decode_1_mread, decode_1_mwrite, decode_1_off_i, decode_1_off_o,
       decode_1_pac_a, decode_1_pac_plus__plus, decode_1_pah_i, decode_1_pah_o, decode_1_pal_i,
       decode_1_pal_o, decode_1_pbc_a, decode_1_pbc_plus__plus, decode_1_pbh_i, decode_1_pbh_o,
       decode_1_pbl_i, decode_1_pbl_o, decode_1_s_a, decode_1_s_rst, decode_1_sel_high, decode_1_sh_i,
       decode_1_sh_o, decode_1_sl, decode_1_sl_i, decode_1_sl_o, decode_1_sl_plus__plus, delay_1_out,
       delay_2_out, delay_3_out, mmu_1_p7, mmu_1_p10, mmu_1_p11, mmu_1_p14, mmu_1_p15, not_1_out, not_2_out,
       not_3_out, not_4_out, not_5_out, or_1_out, or_2_out, or_3_out, reset_1_out;
  wire [3:0] _16_bit_reg_cnt_1_data_out, _16_bit_reg_cnt_1_data_out_2, _16_bit_reg_cnt_2_dbg_2,
       _16_bit_reg_cnt_2_dbg_3, _16_bit_reg_cnt_3_dbg_2, _16_bit_reg_cnt_3_dbg_3, alu_board_1_dbg_a,
       alu_board_1_dbg_a_2, alu_board_1_dbg_b, alu_board_1_dbg_b_2, decode_1_address_2, decode_1_address_3,
       decode_1_dbg, mar_1_dbg_2, mar_1_dbg_3;
  wire [4:0] decode_1_alu_op;
  wire [7:0] _16_bit_reg_cnt_2_dbg, _16_bit_reg_cnt_3_dbg, decode_1_address, mar_1_dbg, mmu_1_p16, mmu_1_p17,
       mmu_1_p18, mmu_1_p19, mmu_1_p20, mmu_1_p21, mmu_1_p22, mmu_1_p23, mmu_1_p24, mmu_1_p25, mmu_1_p26,
       mmu_1_p27;
  wire [7:4] decode_1_dbg_2;
  wire [15:0] _16_bit_reg_cnt_1_dbg;

  Seven_Seg_Hex seven_seg_hex_1 (.d(decode_1_dbg_2), .dp(1'b0));
  not not_1 (not_1_out, decode_1_fault);
  and and_1 (and_1_out, clk, not_1_out);
  Seven_Seg_Hex seven_seg_hex_2 (.d(decode_1_dbg), .dp(1'b0));
  Seven_Seg_Hex seven_seg_hex_3 (.d(_16_bit_reg_cnt_1_data_out_2), .dp(1'b0));
  Seven_Seg_Hex seven_seg_hex_4 (.d(_16_bit_reg_cnt_1_data_out), .dp(1'b0));
  decode decode_1 (
    .RST(reset_1_out), .DATA({_16_bit_reg_cnt_1_data_out_2, _16_bit_reg_cnt_1_data_out}), .clk(and_1_out),
    .C(alu_board_1_c), .Z(alu_board_1_z), .SF(alu_board_1_sf), .OF(alu_board_1_of), .INT(mmu_1_p11),
    .b_o(decode_1_b_o), .sh_o(decode_1_sh_o), .sl_o(decode_1_sl_o), .mh_o(decode_1_mh_o),
    .ml_o(decode_1_ml_o), .off_o(decode_1_off_o), .s_a(decode_1_s_a), .alu_d(decode_1_alu_d),
    .mf_a(decode_1_mf_a), .aluf_d(decode_1_aluf_d), .f_o(decode_1_f_o), .b_i(decode_1_b_i),
    .sh_i(decode_1_sh_i), .sl_i(decode_1_sl_i), .mh_i(decode_1_mh_i), .ml_i(decode_1_ml_i),
    .off_i(decode_1_off_i), .sl(decode_1_sl), .sl_plus__plus(decode_1_sl_plus__plus), .f_i(decode_1_f_i),
    .A_i(decode_1_a_i), .A_o(decode_1_a_o), .MREAD(decode_1_mread), .MWRITE(decode_1_mwrite),
    .pAh_o(decode_1_pah_o), .pAl_o(decode_1_pal_o), .pAh_i(decode_1_pah_i), .pAl_i(decode_1_pal_i),
    .pBc_plus__plus(decode_1_pbc_plus__plus), .pBc_a(decode_1_pbc_a), .pBh_o(decode_1_pbh_o),
    .pBl_o(decode_1_pbl_o), .pBh_i(decode_1_pbh_i), .pBl_i(decode_1_pbl_i),
    .pAc_plus__plus(decode_1_pac_plus__plus), .pAc_a(decode_1_pac_a),
    .Address({decode_1_address_3, decode_1_address_2, decode_1_address}), .ALU_op(decode_1_alu_op),
    .ALU_latch(decode_1_alu_latch), .ei(decode_1_ei), .s_rst(decode_1_s_rst), .di_iv_o(decode_1_di_iv_o),
    .DBG({decode_1_dbg_2, decode_1_dbg}), .FAULT(decode_1_fault), .sel_high(decode_1_sel_high));  // open: NC, NC1, NC2, sel_A
  Seven_Seg_Hex seven_seg_hex_5 (.d(decode_1_address_3), .dp(1'b0));
  Seven_Seg_Hex seven_seg_hex_6 (.d(decode_1_address_2), .dp(1'b0));
  Seven_Seg_Hex seven_seg_hex_7 (.d(decode_1_address[7:4]), .dp(1'b0));
  Seven_Seg_Hex seven_seg_hex_8 (.d(decode_1_address[3:0]), .dp(1'b0));
  _16_bit_reg_cnt _16_bit_reg_cnt_1 (
    .LOW_D(decode_1_sl_o), .HIGH_D(decode_1_sh_o), .OUT_A(decode_1_s_a), .LOW_LD(decode_1_sl_i),
    .HIGH_LD(decode_1_sh_i), .INC(decode_1_sl_plus__plus), .DEC(decode_1_sl), .RST(decode_1_s_rst),
    .DATA({_16_bit_reg_cnt_1_data_out_2, _16_bit_reg_cnt_1_data_out}),
    .DATA_OUT({_16_bit_reg_cnt_1_data_out_2, _16_bit_reg_cnt_1_data_out}),
    .Address({decode_1_address_3, decode_1_address_2, decode_1_address}), .DBG(_16_bit_reg_cnt_1_dbg));
  alu_board alu_board_1 (
    .DATA({_16_bit_reg_cnt_1_data_out_2, _16_bit_reg_cnt_1_data_out}), .A_i(decode_1_a_i),
    .A_o(decode_1_a_o), .ALU_latch(decode_1_alu_latch), .B_i(decode_1_b_i), .B_o(decode_1_b_o),
    .ALU_OP(decode_1_alu_op), .ALU_d(decode_1_alu_d), .ALUF_d(decode_1_aluf_d), .F_o(decode_1_f_o),
    .F_i(decode_1_f_i), .DATA_OUT({_16_bit_reg_cnt_1_data_out_2, _16_bit_reg_cnt_1_data_out}),
    .C(alu_board_1_c), .Z(alu_board_1_z), .SF(alu_board_1_sf), .OF(alu_board_1_of),
    .DBG_A({alu_board_1_dbg_a_2, alu_board_1_dbg_a}), .DBG_B({alu_board_1_dbg_b_2, alu_board_1_dbg_b}));
  mar mar_1 (
    .LOW_D(decode_1_ml_o), .HIGH_D(decode_1_mh_o), .MF_A(decode_1_mf_a), .LOW_LD(decode_1_ml_i),
    .HIGH_LD(decode_1_mh_i), .INC(1'b1), .DEC(1'b1), .RST(reset_1_out),
    .DATA({_16_bit_reg_cnt_1_data_out_2, _16_bit_reg_cnt_1_data_out}), .OFF_i(decode_1_off_i),
    .OFF_o(decode_1_off_o), .sel_high(decode_1_sel_high), .imm(decode_1_alu_op),
    .DATA_OUT({_16_bit_reg_cnt_1_data_out_2, _16_bit_reg_cnt_1_data_out}),
    .Address({decode_1_address_3, decode_1_address_2, decode_1_address}),
    .DBG({mar_1_dbg_3, mar_1_dbg_2, mar_1_dbg}));
  _16_bit_reg_cnt _16_bit_reg_cnt_2 (
    .LOW_D(decode_1_pal_o), .HIGH_D(decode_1_pah_o), .OUT_A(decode_1_pac_a), .LOW_LD(decode_1_pal_i),
    .HIGH_LD(decode_1_pah_i), .INC(decode_1_pac_plus__plus), .DEC(1'b1), .RST(reset_1_out),
    .DATA({_16_bit_reg_cnt_1_data_out_2, _16_bit_reg_cnt_1_data_out}),
    .DATA_OUT({_16_bit_reg_cnt_1_data_out_2, _16_bit_reg_cnt_1_data_out}),
    .Address({decode_1_address_3, decode_1_address_2, decode_1_address}),
    .DBG({_16_bit_reg_cnt_2_dbg_3, _16_bit_reg_cnt_2_dbg_2, _16_bit_reg_cnt_2_dbg}));
  _16_bit_reg_cnt _16_bit_reg_cnt_3 (
    .LOW_D(decode_1_pbl_o), .HIGH_D(decode_1_pbh_o), .OUT_A(decode_1_pbc_a), .LOW_LD(decode_1_pbl_i),
    .HIGH_LD(decode_1_pbh_i), .INC(decode_1_pbc_plus__plus), .DEC(1'b1), .RST(reset_1_out),
    .DATA({_16_bit_reg_cnt_1_data_out_2, _16_bit_reg_cnt_1_data_out}),
    .DATA_OUT({_16_bit_reg_cnt_1_data_out_2, _16_bit_reg_cnt_1_data_out}),
    .Address({decode_1_address_3, decode_1_address_2, decode_1_address}),
    .DBG({_16_bit_reg_cnt_3_dbg_3, _16_bit_reg_cnt_3_dbg_2, _16_bit_reg_cnt_3_dbg}));
  Reset #(.invertOutput("false")) reset_1 (.out(reset_1_out));
  Seven_Seg_Hex seven_seg_hex_9 (.d(alu_board_1_dbg_a_2), .dp(1'b0));
  Seven_Seg_Hex seven_seg_hex_10 (.d(mar_1_dbg_3), .dp(1'b0));
  Seven_Seg_Hex seven_seg_hex_11 (.d(_16_bit_reg_cnt_2_dbg_3), .dp(1'b0));
  Seven_Seg_Hex seven_seg_hex_12 (.d(_16_bit_reg_cnt_3_dbg_3), .dp(1'b0));
  LED led_1 (.in(mmu_1_p15));
  Seven_Seg_Hex seven_seg_hex_13 (.d(alu_board_1_dbg_a), .dp(1'b0));
  Seven_Seg_Hex seven_seg_hex_14 (.d(mar_1_dbg_2), .dp(1'b0));
  Seven_Seg_Hex seven_seg_hex_15 (.d(_16_bit_reg_cnt_2_dbg_2), .dp(1'b0));
  Seven_Seg_Hex seven_seg_hex_16 (.d(_16_bit_reg_cnt_3_dbg_2), .dp(1'b0));
  // MMU mmu_1: pin names not known; wires that end beside it: {_16_bit_reg_cnt_1_data_out_2, _16_bit_reg_cnt_1_data_out}, decode_1_mread, decode_1_mwrite, {decode_1_address_3, decode_1_address_2, decode_1_address}, reset_1_out, decode_1_alu_latch, mmu_1_p7, mmu_1_p25[1], mmu_1_p25[2], mmu_1_p10, mmu_1_p11, decode_1_di_iv_o, decode_1_ei, mmu_1_p14, mmu_1_p15, mmu_1_p16, mmu_1_p17, mmu_1_p18, mmu_1_p19, mmu_1_p20, mmu_1_p21, mmu_1_p22, mmu_1_p23, mmu_1_p24, mmu_1_p25, mmu_1_p26, mmu_1_p27
  or or_1 (or_1_out, mmu_1_p14, decode_1_mwrite);
  or or_2 (or_2_out, mmu_1_p14, decode_1_mread);
  Seven_Seg_Hex seven_seg_hex_17 (.d(alu_board_1_dbg_b_2), .dp(1'b0));
  Seven_Seg_Hex seven_seg_hex_18 (.d(mar_1_dbg[7:4]), .dp(1'b0));
  Seven_Seg_Hex seven_seg_hex_19 (.d(_16_bit_reg_cnt_2_dbg[7:4]), .dp(1'b0));
  Seven_Seg_Hex seven_seg_hex_20 (.d(_16_bit_reg_cnt_3_dbg[7:4]), .dp(1'b0));
  Seven_Seg_Hex seven_seg_hex_21 (.d(alu_board_1_dbg_b), .dp(1'b0));
  Seven_Seg_Hex seven_seg_hex_22 (.d(mar_1_dbg[3:0]), .dp(1'b0));
  Seven_Seg_Hex seven_seg_hex_23 (.d(_16_bit_reg_cnt_2_dbg[3:0]), .dp(1'b0));
  Seven_Seg_Hex seven_seg_hex_24 (.d(_16_bit_reg_cnt_3_dbg[3:0]), .dp(1'b0));
  Seven_Seg_Hex seven_seg_hex_25 (.d(mmu_1_p16[7:4]), .dp(1'b0));
  not not_2 (not_2_out, or_1_out);
  not not_3 (not_3_out, or_2_out);
  Seven_Seg_Hex seven_seg_hex_26 (.d(mmu_1_p16[3:0]), .dp(1'b0));
  Seven_Seg_Hex seven_seg_hex_27 (.d(_16_bit_reg_cnt_1_dbg[15:12]), .dp(1'b0));
  or or_3 (or_3_out, not_2_out, not_3_out);
  Seven_Seg_Hex seven_seg_hex_28 (.d(_16_bit_reg_cnt_1_dbg[11:8]), .dp(1'b0));
  Seven_Seg_Hex seven_seg_hex_29 (.d(_16_bit_reg_cnt_1_dbg[7:4]), .dp(1'b0));
  not not_4 (not_4_out, or_3_out);
  Button button_1 (.out(mmu_1_p25[7]));
  Button button_2 (.out(mmu_1_p25[6]));
  DipSwitch dipswitch_1 (.out(mmu_1_p26[7]));
  DipSwitch dipswitch_2 (.out(mmu_1_p26[6]));
  DipSwitch dipswitch_3 (.out(mmu_1_p27[7]));
  DipSwitch dipswitch_4 (.out(mmu_1_p27[6]));
  Seven_Seg_Hex seven_seg_hex_30 (.d(_16_bit_reg_cnt_1_dbg[3:0]), .dp(1'b0));
  Delay #(.delayTime(5)) delay_1 (.in(not_2_out), .out(delay_1_out));
  Delay #(.delayTime(5)) delay_2 (.in(not_3_out), .out(delay_2_out));
  LightBulb lightbulb_1 (.A(1'b0), .B(mmu_1_p17[7]));
  LightBulb lightbulb_2 (.A(1'b0), .B(mmu_1_p18[7]));
  LightBulb lightbulb_3 (.A(1'b0), .B(mmu_1_p19[7]));
  LightBulb lightbulb_4 (.A(1'b0), .B(mmu_1_p20[7]));
  LightBulb lightbulb_5 (.A(1'b0), .B(mmu_1_p21[7]));
  LightBulb lightbulb_6 (.A(1'b0), .B(mmu_1_p22[7]));
  LightBulb lightbulb_7 (.A(1'b0), .B(mmu_1_p23[7]));
  LightBulb lightbulb_8 (.A(1'b0), .B(mmu_1_p24[7]));
  Button button_3 (.out(mmu_1_p25[5]));
  Button button_4 (.out(mmu_1_p25[4]));
  DipSwitch dipswitch_5 (.out(mmu_1_p26[5]));
  DipSwitch dipswitch_6 (.out(mmu_1_p26[4]));
  DipSwitch dipswitch_7 (.out(mmu_1_p27[5]));
  DipSwitch dipswitch_8 (.out(mmu_1_p27[4]));
  LightBulb lightbulb_9 (.A(1'b0), .B(mmu_1_p17[6]));
  LightBulb lightbulb_10 (.A(1'b0), .B(mmu_1_p17[5]));
  LightBulb lightbulb_11 (.A(1'b0), .B(mmu_1_p18[6]));
  LightBulb lightbulb_12 (.A(1'b0), .B(mmu_1_p18[5]));
  LightBulb lightbulb_13 (.A(1'b0), .B(mmu_1_p19[6]));
  LightBulb lightbulb_14 (.A(1'b0), .B(mmu_1_p19[5]));
  LightBulb lightbulb_15 (.A(1'b0), .B(mmu_1_p20[6]));
  LightBulb lightbulb_16 (.A(1'b0), .B(mmu_1_p20[5]));
  LightBulb lightbulb_17 (.A(1'b0), .B(mmu_1_p21[6]));
  LightBulb lightbulb_18 (.A(1'b0), .B(mmu_1_p21[5]));
  LightBulb lightbulb_19 (.A(1'b0), .B(mmu_1_p22[6]));
  LightBulb lightbulb_20 (.A(1'b0), .B(mmu_1_p22[5]));
  LightBulb lightbulb_21 (.A(1'b0), .B(mmu_1_p23[6]));
  LightBulb lightbulb_22 (.A(1'b0), .B(mmu_1_p23[5]));
  LightBulb lightbulb_23 (.A(1'b0), .B(mmu_1_p24[6]));
  LightBulb lightbulb_24 (.A(1'b0), .B(mmu_1_p24[5]));
  Button button_5 (.out(mmu_1_p25[3]));
  Button button_6 (.out(mmu_1_p25[2]));
  DipSwitch dipswitch_9 (.out(mmu_1_p26[3]));
  DipSwitch dipswitch_10 (.out(mmu_1_p26[2]));
  DipSwitch dipswitch_11 (.out(mmu_1_p27[3]));
  DipSwitch dipswitch_12 (.out(mmu_1_p27[2]));
  LightBulb lightbulb_25 (.A(1'b0), .B(mmu_1_p17[4]));
  LightBulb lightbulb_26 (.A(1'b0), .B(mmu_1_p17[3]));
  LightBulb lightbulb_27 (.A(1'b0), .B(mmu_1_p18[4]));
  LightBulb lightbulb_28 (.A(1'b0), .B(mmu_1_p18[3]));
  LightBulb lightbulb_29 (.A(1'b0), .B(mmu_1_p19[4]));
  LightBulb lightbulb_30 (.A(1'b0), .B(mmu_1_p19[3]));
  LightBulb lightbulb_31 (.A(1'b0), .B(mmu_1_p20[4]));
  LightBulb lightbulb_32 (.A(1'b0), .B(mmu_1_p20[3]));
  LightBulb lightbulb_33 (.A(1'b0), .B(mmu_1_p21[4]));
  LightBulb lightbulb_34 (.A(1'b0), .B(mmu_1_p21[3]));
  LightBulb lightbulb_35 (.A(1'b0), .B(mmu_1_p22[4]));
  LightBulb lightbulb_36 (.A(1'b0), .B(mmu_1_p22[3]));
  LightBulb lightbulb_37 (.A(1'b0), .B(mmu_1_p23[4]));
  LightBulb lightbulb_38 (.A(1'b0), .B(mmu_1_p23[3]));
  LightBulb lightbulb_39 (.A(1'b0), .B(mmu_1_p24[4]));
  LightBulb lightbulb_40 (.A(1'b0), .B(mmu_1_p24[3]));
  Button button_7 (.out(mmu_1_p25[1]));
  Button UP (.out(mmu_1_p25[0]));
  DipSwitch dipswitch_13 (.out(mmu_1_p26[1]));
  DipSwitch dipswitch_14 (.out(mmu_1_p26[0]));
  DipSwitch dipswitch_15 (.out(mmu_1_p27[1]));
  DipSwitch dipswitch_16 (.out(mmu_1_p27[0]));
  Telnet #(.telnetEscape("false"), .port(1234)) telnet_1 (
    .in({_16_bit_reg_cnt_1_data_out_2, _16_bit_reg_cnt_1_data_out}), .C(not_4_out), .wr(delay_1_out),
    .rd(delay_2_out), .out({_16_bit_reg_cnt_1_data_out_2, _16_bit_reg_cnt_1_data_out}), .av(mmu_1_p10));
  LightBulb lightbulb_41 (.A(1'b0), .B(mmu_1_p17[2]));
  LightBulb lightbulb_42 (.A(1'b0), .B(mmu_1_p17[1]));
  LightBulb lightbulb_43 (.A(1'b0), .B(mmu_1_p18[2]));
  LightBulb lightbulb_44 (.A(1'b0), .B(mmu_1_p18[1]));
  LightBulb lightbulb_45 (.A(1'b0), .B(mmu_1_p19[2]));
  LightBulb lightbulb_46 (.A(1'b0), .B(mmu_1_p19[1]));
  LightBulb lightbulb_47 (.A(1'b0), .B(mmu_1_p20[2]));
  LightBulb lightbulb_48 (.A(1'b0), .B(mmu_1_p20[1]));
  LightBulb lightbulb_49 (.A(1'b0), .B(mmu_1_p21[2]));
  LightBulb lightbulb_50 (.A(1'b0), .B(mmu_1_p21[1]));
  LightBulb lightbulb_51 (.A(1'b0), .B(mmu_1_p22[2]));
  LightBulb lightbulb_52 (.A(1'b0), .B(mmu_1_p22[1]));
  LightBulb lightbulb_53 (.A(1'b0), .B(mmu_1_p23[2]));
  LightBulb lightbulb_54 (.A(1'b0), .B(mmu_1_p23[1]));
  LightBulb lightbulb_55 (.A(1'b0), .B(mmu_1_p24[2]));
  LightBulb lightbulb_56 (.A(1'b0), .B(mmu_1_p24[1]));
  LightBulb lightbulb_57 (.A(1'b0), .B(mmu_1_p17[0]));
  LightBulb lightbulb_58 (.A(1'b0), .B(mmu_1_p18[0]));
  LightBulb lightbulb_59 (.A(1'b0), .B(mmu_1_p19[0]));
  LightBulb lightbulb_60 (.A(1'b0), .B(mmu_1_p20[0]));
  LightBulb lightbulb_61 (.A(1'b0), .B(mmu_1_p21[0]));
  LightBulb lightbulb_62 (.A(1'b0), .B(mmu_1_p22[0]));
  LightBulb lightbulb_63 (.A(1'b0), .B(mmu_1_p23[0]));
  LightBulb lightbulb_64 (.A(1'b0), .B(mmu_1_p24[0]));
  not not_5 (not_5_out, mmu_1_p25[0]);
  Delay delay_3 (.in(not_5_out), .out(delay_3_out));
  and and_2 (mmu_1_p7, mmu_1_p25[0], delay_3_out);

  // Notes on the sheet:
  //   clk: Hz: 2147483647
  //   SP
  //   ALU
  //   MAR
  //   PC_a
  //   PC_b
  //   A
  //   BP
  //   PCa
  //   PCb
  //   B
  //   TLB Index
endmodule
